// Logisim project project1.circ as structural Verilog: 2 circuits, main circuit 1b ALU
module _1b_ALU (
  input  A_inv,
  input  B_inv,
  input  C_in,
  input  [1:0] in_4,
  input  A,
  input  B,
  input  Less,
  output Result,
  output Set,
  output Overflow,
  output C_out
);

  wire adder_1_out, and_1_out, or_1_out, xor_1_out, xor_2_out;

  xor xor_1 (xor_1_out, A_inv, A);
  xor xor_2 (xor_2_out, B_inv, B);
  and and_1 (and_1_out, xor_1_out, xor_2_out);
  or or_1 (or_1_out, xor_1_out, xor_2_out);
  Adder #(.width(1)) adder_1 (.a(xor_1_out), .b(xor_2_out), .out(adder_1_out), .cin(C_in), .cout(C_out));
  Multiplexer #(.select(2)) multiplexer_1 (
    .in0(and_1_out), .in1(or_1_out), .in2(adder_1_out), .in3(Less), .out(Result), .sel(in_4));  // open: en
  xor xor_3 (Set, adder_1_out, Overflow);
  xor xor_4 (Overflow, C_in, C_out);
endmodule

module ALU (
  input  [3:0] in_1,
  input  [7:0] A,
  input  [7:0] B,
  output [7:0] out_4,
  output Zero,
  output Overflow
);

  wire n1b_alu_1_c_out, n1b_alu_2_c_out, n1b_alu_3_c_out, n1b_alu_4_c_out, n1b_alu_5_c_out, n1b_alu_6_c_out,
       n1b_alu_7_c_out, n1b_alu_8_set;

  Hex_Digit_Display hex_digit_display_1 (.value(A[3:0]));  // open: dp
  Hex_Digit_Display hex_digit_display_2 (.value(A[7:4]));  // open: dp
  Hex_Digit_Display hex_digit_display_3 (.value(B[7:4]));  // open: dp
  Hex_Digit_Display hex_digit_display_4 (.value(B[3:0]));  // open: dp
  Hex_Digit_Display hex_digit_display_5 (.value(in_1));  // open: dp
  _1b_ALU u_1b_alu_1 (
    .A(A[0]), .B(B[0]), .Less(n1b_alu_8_set), .Result(out_4[0]), .A_inv(in_1[3]), .B_inv(in_1[2]),
    .C_in(in_1[2]), .in_4(in_1[1:0]), .C_out(n1b_alu_1_c_out));  // open: Set, Overflow
  _1b_ALU u_1b_alu_2 (
    .A(A[1]), .B(B[1]), .Less(1'b0), .Result(out_4[1]), .A_inv(in_1[3]), .B_inv(in_1[2]),
    .C_in(n1b_alu_1_c_out), .in_4(in_1[1:0]), .C_out(n1b_alu_2_c_out));  // open: Set, Overflow
  _1b_ALU u_1b_alu_3 (
    .A(A[2]), .B(B[2]), .Less(1'b0), .Result(out_4[2]), .A_inv(in_1[3]), .B_inv(in_1[2]),
    .C_in(n1b_alu_2_c_out), .in_4(in_1[1:0]), .C_out(n1b_alu_3_c_out));  // open: Set, Overflow
  _1b_ALU u_1b_alu_4 (
    .A(A[3]), .B(B[3]), .Less(1'b0), .Result(out_4[3]), .A_inv(in_1[3]), .B_inv(in_1[2]),
    .C_in(n1b_alu_3_c_out), .in_4(in_1[1:0]), .C_out(n1b_alu_4_c_out));  // open: Set, Overflow
  _1b_ALU u_1b_alu_5 (
    .A(A[4]), .B(B[4]), .Less(1'b0), .Result(out_4[4]), .A_inv(in_1[3]), .B_inv(in_1[2]),
    .C_in(n1b_alu_4_c_out), .in_4(in_1[1:0]), .C_out(n1b_alu_5_c_out));  // open: Set, Overflow
  _1b_ALU u_1b_alu_6 (
    .A(A[5]), .B(B[5]), .Less(1'b0), .Result(out_4[5]), .A_inv(in_1[3]), .B_inv(in_1[2]),
    .C_in(n1b_alu_5_c_out), .in_4(in_1[1:0]), .C_out(n1b_alu_6_c_out));  // open: Set, Overflow
  _1b_ALU u_1b_alu_7 (
    .A(A[6]), .B(B[6]), .Less(1'b0), .Result(out_4[6]), .A_inv(in_1[3]), .B_inv(in_1[2]),
    .C_in(n1b_alu_6_c_out), .in_4(in_1[1:0]), .C_out(n1b_alu_7_c_out));  // open: Set, Overflow
  _1b_ALU u_1b_alu_8 (
    .A(A[7]), .B(B[7]), .Less(1'b0), .Result(out_4[7]), .Set(n1b_alu_8_set), .Overflow(Overflow),
    .A_inv(in_1[3]), .B_inv(in_1[2]), .C_in(n1b_alu_7_c_out), .in_4(in_1[1:0]));  // open: C_out
  Hex_Digit_Display hex_digit_display_6 (.value(out_4[7:4]));  // open: dp
  Hex_Digit_Display hex_digit_display_7 (.value(out_4[3:0]));  // open: dp
  nor nor_1 (Zero, out_4[0], out_4[1], out_4[2], out_4[3], out_4[4], out_4[5], out_4[6], out_4[7]);

  // Notes on the sheet:
  //   4-bit ALU control
endmodule
