// Logisim project project2.circ as structural Verilog: 1 circuit, main circuit main
module main (
  input  [2:0] Testcase_Number,
  input  [2:0] Testcase_Number_2,
  output PASS,
  output PASS_2,
  output Finished,
  output Finished_2,
  output [7:0] Multiplicand,
  output [7:0] Multiplier,
  output [7:0] HI,
  output [7:0] LO,
  output [7:0] Dividend__A,
  output [7:0] Divisor__B,
  output [7:0] Remainder__R,
  output [7:0] Quotient__Q
);

  wire and_1_out, and_2_out, and_3_out, and_4_out, and_5_out, and_6_out, and_7_out, and_8_out, and_9_out,
       and_10_out, button_1_out, button_2_out, button_3_out, button_4_out, comparator_3_eq, counter_1_carry,
       counter_2_carry, counter_4_carry, counter_5_carry, not_1_out, not_2_out, not_3_out, not_4_out,
       not_5_out, not_6_out, not_7_out, not_8_out, subtractor_1_bout;
  wire [0:0] adder_1_out, multiplexer_2_out, multiplexer_5_out;
  wire [6:0] multiplexer_2_out_2;
  wire [7:0] adder_1_cout, multiplexer_1_out, register_3_q, register_4_q, subtractor_1_out;
  wire [15:0] rom_1_data, rom_2_data;

  Button button_1 (.out(button_1_out));
  Button button_2 (.out(button_2_out));
  not not_1 (not_1_out, Finished);
  and and_1 (and_1_out, button_2_out, not_1_out);
  Hex_Digit_Display hex_digit_display_1 (.value(Multiplicand[7:4]));  // open: dp
  Hex_Digit_Display hex_digit_display_2 (.value(Multiplicand[3:0]));  // open: dp
  ROM #(.addrWidth(3), .dataWidth(32)) rom_1 (
    .addr(Testcase_Number), .data({Multiplicand, Multiplier, rom_1_data}));  // open: sel
  Hex_Digit_Display hex_digit_display_3 (.value(Multiplier[7:4]));  // open: dp
  Register register_1 (.D(adder_1_cout), .Q(HI), .clk(and_1_out), .clr(button_1_out));  // open: en
  Multiplexer #(.width(8)) multiplexer_1 (
    .in0({8{1'b0}}), .in1(Multiplicand), .out(multiplexer_1_out), .sel(multiplexer_2_out[0]));  // open: en
  not not_2 (not_2_out, counter_1_carry);
  Hex_Digit_Display hex_digit_display_4 (.value(Multiplier[3:0]));  // open: dp
  Adder adder_1 (
    .a(multiplexer_1_out), .b(HI), .out({adder_1_cout[6:0], adder_1_out[0]}), .cout(adder_1_cout[7]));  // open: cin
  and and_2 (and_2_out, button_1_out, not_2_out);
  Comparator #(.width(16)) comparator_1 (.a(rom_1_data), .b({HI, LO}), .eq(PASS));  // open: gt, lt
  Hex_Digit_Display hex_digit_display_5 (.value(HI[7:4]));  // open: dp
  Counter #(.width(1), .max('h1), .trigger("falling")) counter_1 (
    .carry(counter_1_carry), .clk(and_2_out), .clr(button_1_out));  // open: load, D, count, Q
  Hex_Digit_Display hex_digit_display_6 (.value(HI[3:0]));  // open: dp
  Register register_2 (
    .D({adder_1_out[0], multiplexer_2_out_2}), .Q(LO), .clk(and_1_out), .clr(button_1_out));  // open: en
  and and_3 (and_3_out, counter_1_carry, 1'b1);
  Hex_Digit_Display hex_digit_display_7 (.value(LO[7:4]));  // open: dp
  Hex_Digit_Display hex_digit_display_8 (.value(LO[3:0]));  // open: dp
  Multiplexer #(.width(8)) multiplexer_2 (
    .in0(LO), .in1(Multiplier), .out({multiplexer_2_out_2, multiplexer_2_out[0]}), .sel(and_4_out));  // open: en
  and and_4 (and_4_out, and_3_out, not_3_out);
  not not_3 (not_3_out, counter_2_carry);
  Counter #(.width(1), .max('h1)) counter_2 (
    .carry(counter_2_carry), .clk(and_5_out), .clr(button_1_out));  // open: load, D, count, Q
  and and_5 (and_5_out, not_3_out, and_1_out);
  Counter #(.max('h8)) counter_3 (.carry(Finished), .clk(and_1_out), .clr(button_1_out));  // open: load, D, count, Q
  Button button_3 (.out(button_3_out));
  Button button_4 (.out(button_4_out));
  not not_4 (not_4_out, Finished_2);
  Hex_Digit_Display hex_digit_display_9 (.value(Dividend__A[7:4]));  // open: dp
  and and_6 (and_6_out, button_4_out, not_4_out);
  Hex_Digit_Display hex_digit_display_10 (.value(Dividend__A[3:0]));  // open: dp
  Subtractor subtractor_1 (
    .a(register_3_q), .b(Divisor__B), .out(subtractor_1_out), .bout(subtractor_1_bout));  // open: bin
  and and_7 (and_7_out, button_3_out, not_5_out);
  not not_5 (not_5_out, counter_4_carry);
  ROM #(.addrWidth(3), .dataWidth(32)) rom_2 (
    .addr(Testcase_Number_2), .data({Dividend__A, Divisor__B, rom_2_data}));  // open: sel
  Hex_Digit_Display hex_digit_display_11 (.value(Divisor__B[7:4]));  // open: dp
  Hex_Digit_Display hex_digit_display_12 (.value(Divisor__B[3:0]));  // open: dp
  Multiplexer #(.width(8)) multiplexer_3 (
    .in0(subtractor_1_out), .in1(register_3_q), .out(Remainder__R), .sel(subtractor_1_bout));  // open: en
  Register register_3 (
    .D({Remainder__R[6:0], multiplexer_5_out[0]}), .Q(register_3_q), .clk(and_6_out), .clr(button_3_out));  // open: en
  Counter #(.width(1), .max('h1), .trigger("falling")) counter_4 (
    .carry(counter_4_carry), .clk(and_7_out), .clr(button_3_out));  // open: load, D, count, Q
  Comparator #(.width(16)) comparator_2 (.a(rom_2_data), .b({Remainder__R, Quotient__Q}), .eq(PASS_2));  // open: gt, lt
  Hex_Digit_Display hex_digit_display_13 (.value(Remainder__R[3:0]));  // open: dp
  Hex_Digit_Display hex_digit_display_14 (.value(Remainder__R[7:4]));  // open: dp
  Comparator comparator_3 (.a(Divisor__B), .b({8{1'b0}}), .eq(comparator_3_eq));  // open: gt, lt
  not not_6 (not_6_out, subtractor_1_bout);
  and and_8 (and_8_out, counter_4_carry, 1'b1);
  not not_7 (not_7_out, comparator_3_eq);
  Multiplexer multiplexer_4 (
    .in0(not_6_out), .in1(not_7_out), .out(Quotient__Q[0]), .sel(comparator_3_eq));  // open: en
  Multiplexer #(.width(8)) multiplexer_5 (
    .in0(register_4_q), .in1(Dividend__A), .out({multiplexer_5_out[0], Quotient__Q[7:1]}), .sel(and_9_out));  // open: en
  and and_9 (and_9_out, and_8_out, not_8_out);
  not not_8 (not_8_out, counter_5_carry);
  Hex_Digit_Display hex_digit_display_15 (.value(Quotient__Q[3:0]));  // open: dp
  Hex_Digit_Display hex_digit_display_16 (.value(Quotient__Q[7:4]));  // open: dp
  Register register_4 (.D(Quotient__Q), .Q(register_4_q), .clk(and_6_out), .clr(button_3_out));  // open: en
  Counter #(.width(1), .max('h1)) counter_5 (
    .carry(counter_5_carry), .clk(and_10_out), .clr(button_3_out));  // open: load, D, count, Q
  and and_10 (and_10_out, not_8_out, and_6_out);
  Counter #(.max('h8)) counter_6 (.carry(Finished_2), .clk(and_6_out), .clr(button_3_out));  // open: load, D, count, Q

  // Notes on the sheet:
  //   By: Sereyvidya Vireak
  //   1. Enter test case number (0-7)
  //   2. Press RESET button
  //   4. Check if LED "PASS?" is ON
  //   3. Press Clock repeatedly until LED "Finished" is ON
  //   RESET
  //   CLOCK
  //   MULTIPLICATION
  //   contents of rom_1 (hex, n*v repeats v):
  //   fffffe01 ff0000 f00f0e10 905002d 332206c6
  //   1. Enter test case number (0-7)
  //   2. Press RESET button
  //   4. Check if LED "PASS?" is ON
  //   3. Press Clock repeatedly until LED "Finished" is ON
  //   RESET
  //   CLOCK
  //   DIVISION
  //   contents of rom_2 (hex, n*v repeats v):
  //   ffff0001 ff0000 f00f0010 9050401 33221101 aa00aa00
endmodule
